// Logisim project lab 8.circ as structural Verilog: 4 circuits, main circuit ALU
module ALU (
  input  [7:0] \Вход_А ,
  input  in_2,
  input  [7:0] \Вход_B ,
  input  [2:0] in_4,
  output [7:0] \Выход ,
  output [4:0] out_6
);

  wire bitselector_1_out, bitselector_2_out, not_1_out, xnor_1_out, xor_1_out;
  wire [7:0] adder_1_out, and_1_out, multiplexer_1_out, multiplexer_2_out, not_2_out, or_1_out,
       subtractor_1_out;

  // Probe on \Вход_А 
  // Probe on \Вход_B 
  Multiplexer #(.width(8), .enable("false")) multiplexer_1 (
    .in0(\Вход_А ), .in1(\Вход_B ), .out(multiplexer_1_out), .sel(in_2));
  not not_1 (not_1_out, in_2);
  Multiplexer #(.width(8), .enable("false")) multiplexer_2 (
    .in0(\Вход_А ), .in1(\Вход_B ), .out(multiplexer_2_out), .sel(not_1_out));
  Adder adder_1 (.a(multiplexer_1_out), .b(multiplexer_2_out), .out(adder_1_out), .cout(out_6[2]));  // open: cin
  Subtractor subtractor_1 (
    .a(multiplexer_1_out), .b(multiplexer_2_out), .out(subtractor_1_out), .bout(out_6[3]));  // open: bin
  assign not_2_out = ~multiplexer_1_out;  // NOT_Gate not_2, 8 bits wide
  assign and_1_out = multiplexer_1_out & multiplexer_2_out;  // AND_Gate and_1, 8 bits wide
  assign or_1_out = multiplexer_1_out | multiplexer_2_out;  // OR_Gate or_1, 8 bits wide
  BitSelector bitselector_1 (.in(multiplexer_2_out), .out(bitselector_1_out), .sel(3'b111));
  BitSelector bitselector_2 (.in(multiplexer_1_out), .out(bitselector_2_out), .sel(3'b111));
  Multiplexer #(.select(3), .width(8), .enable("false")) multiplexer_3 (
    .in0(multiplexer_1_out), .in1(adder_1_out), .in2(subtractor_1_out), .in3(not_2_out), .in4(and_1_out),
    .in5(or_1_out), .out({out_6[1], \Выход [6:0]}), .sel(in_4));  // open: in6, in7
  // Probe on {out_6[1], \Выход [6:0]}
  nor nor_1 (out_6[0], \Выход [3], \Выход [0], \Выход [1], \Выход [2], \Выход [4], \Выход [5], \Выход [6], out_6[1]);
  xor xor_1 (xor_1_out, out_6[1], bitselector_1_out);
  xnor xnor_1 (xnor_1_out, bitselector_1_out, bitselector_2_out);
  and and_2 (out_6[4], xor_1_out, xnor_1_out);

  assign \Выход [7] = out_6[1];
endmodule

module CPU (
);

  wire and_1_out, bitselector_1_out, clock_1_out, lc2_1_out_2, lc2_1_out_3, not_1_out, not_2_out, Reset_out;
  wire [2:0] lc1_1_out_2;
  wire [3:0] Adress_q, Command_q, Counter_q, multiplexer_1_out;
  wire [3:3] lc1_1_out_2_2;
  wire [7:0] Acc_q, \alu_1_выход , ram_1_data;

  Button Reset (.out(Reset_out));
  not not_1 (not_1_out, lc2_1_out_2);
  Clock clock_1 (.out(clock_1_out));
  Counter #(.width(4), .max('hf)) Counter (
    .load(lc2_1_out_2), .D(Adress_q), .count(not_1_out), .Q(Counter_q), .clk(clock_1_out), .clr(Reset_out));  // open: carry
  Multiplexer #(.width(4), .enable("false")) multiplexer_1 (
    .in0(Counter_q), .in1(Adress_q), .out(multiplexer_1_out), .sel(not_2_out));
  not not_2 (not_2_out, clock_1_out);
  LC2 lc2_1 (.in_1(Command_q), .out_2(lc2_1_out_2), .out_3(lc2_1_out_3));
  RAM #(.addrWidth(4), .bus("separate")) ram_1 (
    .addr(multiplexer_1_out), .din(Acc_q), .data(ram_1_data), .clk(lc2_1_out_3));  // open: str, sel, ld, clr
  Register #(.width(4)) Adress (.D(ram_1_data[3:0]), .Q(Adress_q), .clk(not_2_out), .clr(Reset_out));  // open: en
  LC1 lc1_1 (.in_1(Command_q), .out_2({lc1_1_out_2_2[3], lc1_1_out_2}));
  Register #(.width(4)) Command (.D(ram_1_data[7:4]), .Q(Command_q), .clk(not_2_out), .clr(Reset_out));  // open: en
  ALU alu_1 (
    .\Вход_А (Acc_q), .in_2(lc1_1_out_2_2[3]), .\Вход_B (ram_1_data), .in_4(lc1_1_out_2),
    .\Выход (\alu_1_выход ));  // open: out_6
  BitSelector #(.width(4)) bitselector_1 (.in(Command_q), .out(bitselector_1_out), .sel(2'b00));
  Register Acc (.D(\alu_1_выход ), .Q(Acc_q), .clk(and_1_out), .clr(Reset_out));  // open: en
  and and_1 (and_1_out, bitselector_1_out, clock_1_out);

  // Notes on the sheet:
  //   LOAD 0001 1
  //   JUMP 0010 2
  //   SUM 0011 3
  //   WRITE 0100 4
  //   SUB 0101 5
  //   OR 1001 9
  //   AND 1011 B
  //   NOT 1101 D
endmodule

module LC1 (
  input  [3:0] in_1,
  output [3:0] out_2
);

  wire and_3_out, and_4_out, not_1_out, not_2_out, not_3_out, not_4_out, not_5_out, not_6_out;

  not not_1 (not_1_out, in_1[3]);
  not not_2 (not_2_out, in_1[2]);
  not not_3 (not_3_out, in_1[1]);
  not not_4 (not_4_out, in_1[2]);
  not not_5 (not_5_out, in_1[3]);
  not not_6 (not_6_out, in_1[1]);
  and and_1 (out_2[3], not_1_out, not_2_out, not_3_out);
  and and_2 (out_2[2], in_1[3], not_4_out);
  and and_3 (and_3_out, not_5_out, in_1[1]);
  and and_4 (and_4_out, in_1[3], not_6_out);
  or or_1 (out_2[0], and_3_out, and_4_out);

  assign out_2[1] = in_1[2];
endmodule

module LC2 (
  input  [3:0] in_1,
  output out_2,
  output out_3
);

  and and_1 (out_2, ~in_1[0], in_1[1], ~in_1[2], ~in_1[3]);  // AND_Gate
  and and_2 (out_3, ~in_1[0], ~in_1[1], in_1[2], ~in_1[3]);  // AND_Gate
endmodule
